// Logisim project lab task 7.circ as structural Verilog: 1 circuit, main circuit main
module main (
  input  in_1,
  input  in_2,
  input  in_3,
  input  in_4,
  input  in_5,
  input  in_6,
  input  in_7,
  input  in_8,
  input  in_9
);

  wire and_1_out, and_2_out, not_1_out, not_2_out, not_3_out, or_1_out, or_2_out;

  not not_1 (not_1_out, in_9);
  LED led_1 (.in(not_1_out));
  and and_1 (and_1_out, in_1, in_2);
  LED led_2 (.in(and_1_out));
  LED led_3 (.in(or_1_out));
  or or_1 (or_1_out, in_5, in_6);
  and and_2 (and_2_out, in_3, in_4);
  or or_2 (or_2_out, in_7, in_8);
  not not_2 (not_2_out, and_2_out);
  not not_3 (not_3_out, or_2_out);
  LED led_4 (.in(not_2_out));
  LED led_5 (.in(not_3_out));

  // Notes on the sheet:
  //   AND GATE
  //   OR GATE
  //   NOT GATE
  //   NOR GATE
  //   NAND GATE
endmodule
